// Logisim project decoder_to_mux_huge.circ as structural Verilog: 1 circuit, main circuit main
module main (
  input  in_1,
  input  in_2,
  input  in_3,
  input  in_4,
  input  in_5,
  input  in_6,
  input  in_7,
  input  in_8,
  input  in_9,
  input  in_10,
  input  in_11,
  input  in_12,
  input  in_13,
  input  in_14,
  input  in_15,
  input  in_16,
  input  in_17,
  input  [3:0] in_18,
  output out_19
);

  wire and_1_out, and_2_out, and_3_out, and_4_out, and_5_out, and_6_out, and_7_out, and_8_out, and_9_out,
       and_10_out, and_11_out, and_12_out, and_13_out, and_14_out, and_15_out, and_16_out, decoder_1_out0,
       decoder_1_out1, decoder_1_out2, decoder_1_out3, decoder_1_out5, decoder_1_out6, decoder_1_out7,
       decoder_1_out8, decoder_1_out9, decoder_1_out10, decoder_1_out11, decoder_1_out12, decoder_1_out13,
       decoder_1_out14, decoder_1_out15;

  Decoder #(.select(4)) decoder_1 (
    .out0(decoder_1_out0), .out1(decoder_1_out1), .out2(decoder_1_out2), .out3(decoder_1_out3), .out4(in_16),
    .out5(decoder_1_out5), .out6(decoder_1_out6), .out7(decoder_1_out7), .out8(decoder_1_out8),
    .out9(decoder_1_out9), .out10(decoder_1_out10), .out11(decoder_1_out11), .out12(decoder_1_out12),
    .out13(decoder_1_out13), .out14(decoder_1_out14), .out15(decoder_1_out15), .sel(in_18), .en(in_17));
  and and_1 (and_1_out, in_1, decoder_1_out0);
  and and_2 (and_2_out, in_2, decoder_1_out1);
  and and_3 (and_3_out, in_3, decoder_1_out2);
  and and_4 (and_4_out, in_4, decoder_1_out3);
  and and_5 (and_5_out, in_5, in_16);
  and and_6 (and_6_out, in_6, decoder_1_out5);
  and and_7 (and_7_out, in_7, decoder_1_out6);
  and and_8 (and_8_out, in_8, decoder_1_out7);
  and and_9 (and_9_out, in_9, decoder_1_out8);
  and and_10 (and_10_out, in_10, decoder_1_out9);
  and and_11 (and_11_out, in_11, decoder_1_out10);
  and and_12 (and_12_out, in_12, decoder_1_out11);
  and and_13 (and_13_out, in_13, decoder_1_out12);
  and and_14 (and_14_out, in_14, decoder_1_out13);
  and and_15 (and_15_out, in_15, decoder_1_out14);
  and and_16 (and_16_out, in_16, decoder_1_out15);
  or or_1 (out_19, and_1_out, and_2_out, and_3_out, and_4_out, and_5_out, and_6_out, and_7_out, and_8_out, and_9_out, and_10_out, and_11_out, and_12_out, and_13_out, and_14_out, and_15_out, and_16_out);
endmodule
