// Logisim project alotof.circ as structural Verilog: 1 circuit, main circuit main
module main (
  input  in_1,
  input  in_2,
  input  in_3,
  input  in_4,
  input  in_5,
  input  in_6,
  input  in_7,
  input  in_8,
  input  in_9,
  input  in_10,
  input  in_11,
  input  in_12,
  input  in_13,
  input  in_14,
  input  in_15,
  input  in_16,
  input  in_17,
  input  in_18,
  input  in_19,
  input  in_20,
  input  in_21
);

  wire and_1_out, and_2_out, and_3_out, and_4_out, and_5_out, and_6_out, and_7_out, and_8_out, and_9_out,
       and_10_out, and_11_out, and_12_out, nand_1_out, nand_2_out, nand_3_out, nand_4_out, not_1_out,
       not_2_out, not_3_out, not_4_out, not_5_out, not_6_out, not_7_out, not_8_out, not_9_out, not_10_out,
       not_11_out, not_12_out, not_13_out, not_14_out, not_15_out, not_16_out, not_17_out, not_18_out,
       not_19_out, not_20_out, not_21_out, not_22_out, or_1_out, or_2_out, or_3_out, or_4_out, or_5_out,
       or_6_out;

  not not_1 (not_1_out, in_1);
  not not_2 (not_2_out, in_2);
  nand nand_1 (nand_1_out, in_4, in_6);
  not not_3 (not_3_out, in_7);
  not not_4 (not_4_out, in_9);
  not not_5 (not_5_out, in_12);
  not not_6 (not_6_out, in_13);
  not not_7 (not_7_out, in_12);
  not not_8 (not_8_out, in_15);
  not not_9 (not_9_out, in_17);
  not not_10 (not_10_out, in_18);
  not not_11 (not_11_out, in_20);
  not not_12 (not_12_out, in_21);
  and and_1 (and_1_out, not_1_out, not_2_out);
  nand nand_2 (nand_2_out, in_4, nand_1_out);
  nand nand_3 (nand_3_out, nand_1_out, in_6);
  or or_1 (or_1_out, not_3_out, not_4_out);
  and and_2 (and_2_out, in_10, not_5_out, not_6_out);
  and and_3 (and_3_out, in_10, not_7_out, in_13);
  and and_4 (and_4_out, not_8_out, not_9_out, not_10_out);
  and and_5 (and_5_out, in_15, in_17, in_18);
  and and_6 (and_6_out, in_19, not_11_out, not_12_out);
  and and_7 (and_7_out, in_19, in_20, in_21);
  not not_13 (not_13_out, and_1_out);
  not not_14 (not_14_out, or_1_out);
  LED led_1 (.in(not_13_out));
  nand nand_4 (nand_4_out, nand_2_out, nand_3_out);
  LED led_2 (.in(not_14_out));
  or or_2 (or_2_out, and_2_out, and_3_out);
  or or_3 (or_3_out, and_4_out, and_5_out);
  LED led_3 (.in(or_3_out));
  or or_4 (or_4_out, and_6_out, and_7_out);
  LED led_4 (.in(or_4_out));
  LED led_5 (.in(nand_4_out));
  LED led_6 (.in(or_2_out));
  not not_15 (not_15_out, in_3);
  not not_16 (not_16_out, in_5);
  not not_17 (not_17_out, in_8);
  and and_8 (and_8_out, not_15_out, not_16_out, in_8);
  and and_9 (and_9_out, in_3, in_5, not_17_out);
  not not_18 (not_18_out, in_11);
  not not_19 (not_19_out, in_14);
  and and_10 (and_10_out, not_18_out, not_19_out, in_16);
  not not_20 (not_20_out, in_14);
  and and_11 (and_11_out, in_11, not_20_out, not_21_out);
  not not_21 (not_21_out, in_16);
  not not_22 (not_22_out, in_16);
  and and_12 (and_12_out, in_11, in_14, not_22_out);
  or or_5 (or_5_out, and_8_out, and_9_out);
  LED led_7 (.in(or_5_out));
  or or_6 (or_6_out, and_10_out, and_11_out, and_12_out);
  LED led_8 (.in(or_6_out));
endmodule
