// Logisim project decoder.circ as structural Verilog: 1 circuit, main circuit main
module main (
  input  in_1,
  input  in_2,
  output O0,
  output O1,
  output O2,
  output O3
);

  wire not_1_out, not_2_out, not_3_out, not_4_out;

  not not_1 (not_1_out, in_1);
  not not_2 (not_2_out, in_2);
  not not_3 (not_3_out, in_1);
  not not_4 (not_4_out, in_2);
  and and_1 (O0, not_1_out, not_2_out);
  and and_2 (O1, not_3_out, in_2);
  and and_3 (O2, in_1, not_4_out);
  and and_4 (O3, in_1, in_2);
endmodule
