// Logisim project decoder_to_demux.circ as structural Verilog: 1 circuit, main circuit main
module main (
  input  in_1,
  input  in_2,
  input  [1:0] in_3,
  output out_4,
  output out_5,
  output out_6,
  output out_7
);

  wire decoder_1_out0, decoder_1_out1, decoder_1_out2, decoder_1_out3;

  Decoder #(.select(2)) decoder_1 (
    .out0(decoder_1_out0), .out1(decoder_1_out1), .out2(decoder_1_out2), .out3(decoder_1_out3), .sel(in_3),
    .en(in_2));
  and and_1 (out_4, decoder_1_out0, in_1);
  and and_2 (out_5, decoder_1_out1, in_1);
  and and_3 (out_6, decoder_1_out2, in_1);
  and and_4 (out_7, decoder_1_out3, in_1);
endmodule
