// Logisim project decoder_to_mux.circ as structural Verilog: 1 circuit, main circuit main
module main (
  input  in_1,
  input  in_2,
  input  in_3,
  input  in_4,
  input  in_5,
  input  [1:0] in_6,
  output out_7
);

  wire and_1_out, and_2_out, and_3_out, and_4_out, decoder_1_out0, decoder_1_out1, decoder_1_out2,
       decoder_1_out3;

  Decoder #(.select(2)) decoder_1 (
    .out0(decoder_1_out0), .out1(decoder_1_out1), .out2(decoder_1_out2), .out3(decoder_1_out3), .sel(in_6),
    .en(in_5));
  and and_1 (and_1_out, in_1, decoder_1_out0);
  and and_2 (and_2_out, in_2, decoder_1_out1);
  and and_3 (and_3_out, in_3, decoder_1_out2);
  and and_4 (and_4_out, in_4, decoder_1_out3);
  or or_1 (out_7, and_1_out, and_2_out, and_3_out, and_4_out);
endmodule
