// Logisim project fun.circ as structural Verilog: 1 circuit, main circuit main
module main (
  input  S,
  input  in_2,
  input  in_3,
  input  in_4,
  input  in_5,
  input  in_6,
  input  in_7,
  output O
);

  wire and_1_out, and_2_out, and_3_out, and_4_out, button_1_out, button_2_out, clock_1_out, clock_2_out,
       clock_3_out, not_1_out, or_2_out;

  Button button_1 (.out(button_1_out));
  not not_1 (not_1_out, button_1_out);
  LED led_1 (.in(and_2_out));
  LED led_2 (.in(and_2_out));
  LED led_3 (.in(and_2_out));
  LED led_4 (.in(and_2_out));
  LED led_5 (.in(and_2_out));
  LED led_6 (.in(and_2_out));
  and and_1 (and_1_out, O, not_1_out);
  LED led_7 (.in(and_2_out));
  LED led_8 (.in(and_2_out));
  LED led_9 (.in(and_2_out));
  LED led_10 (.in(and_2_out));
  LED led_11 (.in(and_2_out));
  LED led_12 (.in(and_2_out));
  LED led_13 (.in(and_2_out));
  LED led_14 (.in(and_2_out));
  LED led_15 (.in(or_2_out));
  LED led_16 (.in(or_2_out));
  LED led_17 (.in(in_3));
  LED led_18 (.in(in_3));
  LED led_19 (.in(in_3));
  LED led_20 (.in(in_3));
  LED led_21 (.in(in_3));
  LED led_22 (.in(in_3));
  LED led_23 (.in(in_4));
  LED led_24 (.in(in_4));
  LED led_25 (.in(and_3_out));
  LED led_26 (.in(and_3_out));
  LED led_27 (.in(and_3_out));
  LED led_28 (.in(and_3_out));
  LED led_29 (.in(and_3_out));
  LED led_30 (.in(and_3_out));
  and and_2 (and_2_out, in_7, clock_1_out);
  LED led_31 (.in(and_2_out));
  LED led_32 (.in(and_2_out));
  or or_1 (O, and_1_out, S);
  LED led_33 (.in(or_2_out));
  LED led_34 (.in(in_3));
  LED led_35 (.in(in_3));
  LED led_36 (.in(in_3));
  LED led_37 (.in(in_4));
  LED led_38 (.in(and_3_out));
  LED led_39 (.in(and_3_out));
  and and_3 (and_3_out, in_5, clock_3_out);
  LED led_40 (.in(and_3_out));
  Clock #(.lowDuration(4)) clock_1 (.out(clock_1_out));
  LED led_41 (.in(and_2_out));
  LED led_42 (.in(and_2_out));
  LED led_43 (.in(and_2_out));
  LED led_44 (.in(and_2_out));
  Button button_2 (.out(button_2_out));
  or or_2 (or_2_out, in_2, button_2_out);
  Clock #(.highDuration(6), .lowDuration(6)) clock_2 (.out(clock_2_out));
  Clock #(.highDuration(6), .lowDuration(6)) clock_3 (.out(clock_3_out));
  LED led_45 (.in(and_2_out));
  LED led_46 (.in(and_2_out));
  LED led_47 (.in(and_2_out));
  LED led_48 (.in(and_2_out));
  LED led_49 (.in(and_2_out));
  LED led_50 (.in(and_2_out));
  LED led_51 (.in(and_2_out));
  LED led_52 (.in(and_2_out));
  LED led_53 (.in(or_2_out));
  LED led_54 (.in(or_2_out));
  LED led_55 (.in(in_3));
  LED led_56 (.in(in_3));
  LED led_57 (.in(in_3));
  LED led_58 (.in(in_3));
  LED led_59 (.in(in_3));
  LED led_60 (.in(in_3));
  LED led_61 (.in(in_4));
  LED led_62 (.in(in_4));
  LED led_63 (.in(and_4_out));
  LED led_64 (.in(and_4_out));
  and and_4 (and_4_out, in_6, clock_2_out);
  LED led_65 (.in(and_4_out));
  LED led_66 (.in(and_4_out));
  LED led_67 (.in(and_4_out));
  LED led_68 (.in(and_4_out));
  LED led_69 (.in(and_2_out));
  LED led_70 (.in(and_2_out));
  LED led_71 (.in(and_2_out));
  LED led_72 (.in(and_2_out));
  LED led_73 (.in(or_2_out));
  LED led_74 (.in(in_3));
  LED led_75 (.in(in_3));
  LED led_76 (.in(in_3));
  LED led_77 (.in(in_4));
  LED led_78 (.in(and_4_out));
  LED led_79 (.in(and_4_out));
  LED led_80 (.in(and_4_out));

  // Notes on the sheet:
  //   R
endmodule
