// Logisim project mux_demux_clocks.circ as structural Verilog: 1 circuit, main circuit main
module main (
  input  in_1,
  input  [1:0] in_2,
  output out_3,
  output out_4,
  output out_5,
  output out_6
);

  wire clock_1_out, clock_2_out, multiplexer_1_out;

  Clock clock_1 (.out(clock_1_out));
  Clock #(.highDuration(4), .lowDuration(4)) clock_2 (.out(clock_2_out));
  Multiplexer multiplexer_1 (.in0(clock_1_out), .in1(clock_2_out), .out(multiplexer_1_out), .sel(in_1));  // open: en
  Demultiplexer #(.select(2)) demultiplexer_1 (
    .out0(out_3), .out1(out_4), .out2(out_5), .out3(out_6), .in(multiplexer_1_out), .sel(in_2));  // open: en
endmodule
